# Fritzing sketch carte_elec (saved by Fritzing 0.9.3b)
breadboards: 1

parts:
  Raspberry_Pi_1 = Raspberry Pi 3 [part_number=RPI-3-V1.2]
  S1 = Pushbutton [package="[THT]"]
  S2 = Pushbutton [package="[THT]"]
  S3 = Pushbutton [package="[THT]"]
  LED1 = LED - 5mm [color="Red (633nm)" package="5 mm [THT]"]

nets:
  N1: Raspberry_Pi_1.GPIO5, Raspberry_Pi_1.GPIO13, Raspberry_Pi_1.GND, S1.Pin_1, S1.Pin_2, S1.Pin_3, S1.Pin_4, S2.Pin_1, S2.Pin_2, S3.Pin_1, S3.Pin_2, S3.Pin_3, S3.Pin_4, LED1.cathode
  N2: Raspberry_Pi_1.GPIO6, S2.Pin_3, S2.Pin_4
  N3: Raspberry_Pi_1.GPIO21, LED1.anode

notes:
  <<prev snap next>>
